# Fritzing sketch Combinazione_Leds_Bottoni (saved by Fritzing 0.9.3b)
breadboards: 1

parts:
  Part1 = Arduino Uno (Rev3)
  S1 = Pushbutton [package="[THT]"]
  S2 = Pushbutton [package="[THT]"]
  R1 = Resistor [tolerance=±5% resistance=10k package=THT]
  R2 = Resistor [tolerance=±5% resistance=10k package=THT]
  R3 = Resistor [tolerance=±5% resistance=220 package=THT]
  LED1 = LED - 5mm [color="Red (633nm)" package="5 mm [THT]"]
  LED2 = LED - 5mm [color="Red (633nm)" package="5 mm [THT]"]
  R4 = Resistor [tolerance=±5% resistance=220 package=THT]
  R5 = Resistor [tolerance=±5% resistance=220 package=THT]
  LED3 = LED - 5mm [color="Red (633nm)" package="5 mm [THT]"]

nets:
  N1: Part1.D8, S1.Pin_1, S1.Pin_2, R1.Pin_0
  N2: Part1.GND, R1.Pin_1, R2.Pin_1, LED1.anode, LED2.anode
  N3: Part1.D2, R3.Pin_0
  N4: Part1.D3_PWM, R4.Pin_0
  N5: Part1.D4, R5.Pin_0
  N6: Part1.D7, S2.Pin_1, S2.Pin_2, R2.Pin_0
  N7: Part1.5V, S1.Pin_3, S1.Pin_4, S2.Pin_3, S2.Pin_4, LED3.anode
  N8: R3.Pin_1, LED1.cathode
  N9: LED2.cathode, R4.Pin_1
