# Fritzing sketch Single power (saved by Fritzing 0.9.3b)
breadboards: 1

parts:
  IC1 = L293D [package=THT]
  Part1 = Arduino Uno (Rev3)

nets:
  N1: IC1.0V, Part1.GND
  N2: IC1.+Vmotor, Part1.VIN
  N3: IC1.Enable_2, Part1.D12/MISO
  N4: IC1.In_3, Part1.D5_PWM
  N5: IC1.In_4, Part1.D6_PWM
  N6: IC1.+V, Part1.5V

notes:
  Davide Gariselli 22/6/2016
  Singola alimentazione, jack
