# Fritzing sketch LoRa_Sketch (saved by Fritzing 0.9.3b)
breadboards: 1

parts:
  Part1 = Arduino Pro Mini (5V)
  BB1 = 4-Line Bi-Directional Level Shifter
  U1 = mystery part, 16 pins [chip_label="LoRa rf96"]

nets:
  N1: Part1.MISO, U1.pin2
  N2: BB1.LV, U1.pin13
  N3: BB1.A1, U1.pin14
  N4: BB1.A2, U1.pin4
  N5: BB1.A3, U1.pin3
  N6: BB1.A4, U1.pin5
  N7: BB1.GND, U1.pin1

notes:
  FTDI 5v
  3v3

custom parts:
  4-Line Bi-Directional Level Shifter: 4-Channel Bi-Directional Level Shifter
